# Fritzing sketch Final Schema (saved by Fritzing 0.8.7b)

parts:
  Part1 = 16-Channel 12-bit PCA9685 PWM/Servo Driver
  J1 = Basic Servo
  J2 = Basic Servo
  J3 = Basic Servo
  VCC1 = Battery block 9V
  Raspberry_Pi_1 = Raspberry Pi 4 [part_number=RPI-4-b]
  J5 = Basic Servo
  J6 = Basic Servo
  J7 = Basic Servo
  J8 = Basic Servo

nets:
  N1: Part1.PWRIN, VCC1.+
  GND: Part1.GND, J1.gnd, J2.gnd, J3.gnd, VCC1.-, Raspberry_Pi_1.GND, J5.gnd, J6.gnd, J7.gnd, J8.gnd
  N2: Part1.0, J3.pulse
  N3: Part1.1, J2.pulse
  VCC: Part1.V+, J1.vcc, J2.vcc, J3.vcc, J5.vcc, J6.vcc, J7.vcc, J8.vcc
  N4: Part1.2, J1.pulse
  N5: Part1.3, J5.pulse
  N6: Part1.4, J7.pulse
  N7: Part1.5, J6.pulse
  N8: Part1.6, J8.pulse
  VCC_2: Part1.VCC, Raspberry_Pi_1.3v3
  N9: Part1.SDA, Raspberry_Pi_1.GPIO2
  N10: Part1.SCL, Raspberry_Pi_1.GPIO3

custom parts:
  16-Channel 12-bit PCA9685 PWM/Servo Driver: The Adafruit 16-Channel 12-bit PWM/Servo Driver will drive up to 16 servos over I2C with only 2 pins. The on-board PCA9685 PWM controller will drive all 16 channels simultaneously with no additional processing overhead. What's more, you can chain up to 62 of them to control up to 992 servos - all with the same 2 pins
  Raspberry Pi 4: The RPi4, a faster version of the awesome Raspberry Pi 2 B ARM Board with 40 pin gpio. Ready for special Raspberry Pi B+ and RPi2 Hat (Hardware attached (on) top)
